# Fritzing sketch Apnea_det (saved by Fritzing 0.9.3b)
circuit board: 5.75827cm x 5.17781cm

parts:
  NANO = Arduino Nano (Rev3.0)
  Componente2 = Triple Axis Accelerometer Breakout - ADXL345 [part_number=ADXL345]
  Componente3 = Bluetooth HC-05 Macho [part_number=HC-05]
  ZS-042_RTC1 = ZS-042 RTC Module [part_number="RTC DS3231"]
  R1 = Resistor [tolerance=±5% resistance=4.7k package=THT]
  R2 = Resistor [tolerance=±5% resistance=4.7k package=THT]
  Q1 = NPN-Transistor [part_number="BT ENABLE" package="TO92 [THT]"]
  R3 = Resistor [tolerance=±5% resistance=1k package=THT]
  R4 = Resistor [tolerance=±5% resistance=1k package=THT]
  R5 = Resistor [tolerance=±5% resistance=1k package=THT]
  R6 = Resistor [tolerance=±5% resistance=1k package=THT]
  R7 = Resistor [tolerance=±5% resistance=1k package=THT]
  R8 = Resistor [tolerance=±5% resistance=1k package=THT]
  LED1 = LED - 5mm [color="Green (560nm)" part_number=INACTIVIDAD package="5 mm [THT]"]
  LED2 = LED - 5mm [color="Blue (505nm)" part_number=BLUETOOTH package="5 mm [THT]"]
  R9 = Resistor [tolerance=±5% resistance=1k package=THT]
  R10 = Resistor [tolerance=±5% resistance=1k package=THT]
  S2 = Pushbutton [part_number="CONEXION BT" package="[THT]"]
  C2 = Ceramic Capacitor [capacitance=100nF package="100 mil [THT, multilayer]"]
  J2 = Piezo Speaker [part_number=BUZZER]
  R11 = Resistor [tolerance=±5% resistance=10k package=THT]
  VCC1 = Battery block 9V

nets:
  N1: NANO.D1/TX, R8.Pin_0
  N2: NANO.D0/RX, R5.Pin_0
  GND: NANO.GND, Componente2.GND, Componente2.SDO, Componente3.GND, ZS-042_RTC1.GND, R3.Pin_1, R6.Pin_1, R9.Pin_1, R10.Pin_1, S2.Pin_3, S2.Pin_4, C2.0, J2.pin1, VCC1.-
  N3: NANO.D2, Componente2.INT1
  N4: NANO.D3, S2.Pin_1, S2.Pin_2, C2.1, R11.Pin_0
  N5: NANO.D4, LED2.anode
  N6: NANO.D5, LED1.anode, J2.pin2
  N7: NANO.VIN, VCC1.+
  N8: NANO.5V, Q1.C, R11.Pin_1
  N9: NANO.A5, Componente2.SCL, ZS-042_RTC1.SCL, R2.Pin_0
  N10: NANO.A4, Componente2.SDA, ZS-042_RTC1.SDA, R1.Pin_0
  N11: NANO.A0, Q1.B
  VCC: NANO.3V3, Componente2.VCC, Componente2.CS, ZS-042_RTC1.VCC, R1.Pin_1, R2.Pin_1
  N12: Componente3.TXD, R4.Pin_0, R5.Pin_1
  N13: Componente3.RXD, R7.Pin_0, R8.Pin_1
  N14: Componente3.VCC, Q1.E
  N15: R3.Pin_0, R4.Pin_1
  N16: R6.Pin_0, R7.Pin_1
  N17: LED1.cathode, R10.Pin_0
  N18: LED2.cathode, R9.Pin_0
